# Fritzing sketch Montagem Básica (saved by Fritzing 0.9.2b)

parts:
  Componente1 = Arduino Uno (Rev3)
  S1 = H-Bridge with L298N
  M1 = DC Motor  # not connected
  J1 = Basic Servo
  VCC1 = Battery block 9V
  M2 = DC Motor
  Componente2 = SRF05 Ultrasonic Rangefinder

nets:
  N1: Componente1.D9_PWM, J1.pulse
  N2: Componente1.D11_PWM/MOSI, S1.IN1
  GND: Componente1.GND, S1.GND, J1.gnd, VCC1.-, Componente2.GND
  N3: Componente1.D0/RX, Componente2.Trig
  N4: Componente1.D1/TX, Componente2.Echo
  N5: Componente1.D3_PWM, S1.IN2
  N6: Componente1.D5_PWM, S1.IN4
  N7: Componente1.D6_PWM, S1.IN3
  VCC: Componente1.5V, J1.vcc, Componente2.VCC
  N8: S1.12V, VCC1.+
  N9: S1.OUT4-Motor2, M2.pin_1

custom parts:
  H-Bridge with L298N: h-bridge
